// Logisim project asynchronous counter.circ as structural Verilog: 1 circuit, main circuit main
module main (
  input  \_0___상향 ,
  output out_2,
  output out_3,
  output out_4,
  output out_5,
  output out_6,
  output out_7,
  output out_8,
  output out_9,
  output out_10,
  output out_11,
  output out_12,
  output out_13,
  output out_14,
  output out_15,
  output out_16,
  output out_17
);

  wire and_1_out, and_2_out, clock_1_out, clock_2_out, clock_3_out, clock_4_out, j_k_ff_2_qn, j_k_ff_5_qn,
       j_k_ff_10_qn, multiplexer_1_out, multiplexer_2_out, multiplexer_3_out;

  Clock clock_1 (.out(clock_1_out));
  Clock clock_2 (.out(clock_2_out));
  Clock clock_3 (.out(clock_3_out));
  J_K_Flip_Flop #(.trigger("falling")) j_k_ff_1 (
    .J(1'b1), .clk(clock_1_out), .K(1'b1), .Q(out_2));  // open: Qn, preset, en, reset
  J_K_Flip_Flop #(.trigger("falling")) j_k_ff_2 (
    .J(1'b1), .clk(clock_2_out), .K(1'b1), .Q(out_6), .Qn(j_k_ff_2_qn));  // open: preset, en, reset
  J_K_Flip_Flop #(.trigger("falling")) j_k_ff_3 (
    .J(1'b1), .clk(clock_3_out), .K(1'b1), .Q(out_10), .reset(and_1_out));  // open: Qn, preset, en
  J_K_Flip_Flop #(.trigger("falling")) j_k_ff_4 (
    .J(1'b1), .clk(out_2), .K(1'b1), .Q(out_3));  // open: Qn, preset, en, reset
  J_K_Flip_Flop #(.trigger("falling")) j_k_ff_5 (
    .J(1'b1), .clk(multiplexer_1_out), .K(1'b1), .Q(out_7), .Qn(j_k_ff_5_qn));  // open: preset, en, reset
  Multiplexer multiplexer_1 (.in0(out_6), .in1(j_k_ff_2_qn), .out(multiplexer_1_out), .sel(\_0___상향 ));  // open: en
  J_K_Flip_Flop #(.trigger("falling")) j_k_ff_6 (
    .J(1'b1), .clk(out_10), .K(1'b1), .Q(out_11), .reset(and_1_out));  // open: Qn, preset, en
  J_K_Flip_Flop #(.trigger("falling")) j_k_ff_7 (
    .J(1'b1), .clk(out_3), .K(1'b1), .Q(out_4));  // open: Qn, preset, en, reset
  Multiplexer multiplexer_2 (.in0(out_7), .in1(j_k_ff_5_qn), .out(multiplexer_2_out), .sel(\_0___상향 ));  // open: en
  J_K_Flip_Flop #(.trigger("falling")) j_k_ff_8 (
    .J(1'b1), .clk(out_11), .K(1'b1), .Q(out_12), .reset(and_1_out));  // open: Qn, preset, en
  J_K_Flip_Flop #(.trigger("falling")) j_k_ff_9 (
    .J(1'b1), .clk(out_4), .K(1'b1), .Q(out_5));  // open: Qn, preset, en, reset
  J_K_Flip_Flop #(.trigger("falling")) j_k_ff_10 (
    .J(1'b1), .clk(multiplexer_2_out), .K(1'b1), .Q(out_8), .Qn(j_k_ff_10_qn));  // open: preset, en, reset
  Multiplexer multiplexer_3 (.in0(out_8), .in1(j_k_ff_10_qn), .out(multiplexer_3_out), .sel(\_0___상향 ));  // open: en
  J_K_Flip_Flop #(.trigger("falling")) j_k_ff_11 (
    .J(1'b1), .clk(out_12), .K(1'b1), .Q(out_13), .reset(and_1_out));  // open: Qn, preset, en
  Hex_Digit_Display hex_digit_display_1 (.value({out_5, out_4, out_3, out_2}));  // open: dp
  J_K_Flip_Flop #(.trigger("falling")) j_k_ff_12 (
    .J(1'b1), .clk(multiplexer_3_out), .K(1'b1), .Q(out_9));  // open: Qn, preset, en, reset
  Hex_Digit_Display hex_digit_display_2 (.value({out_13, out_12, out_11, out_10}));  // open: dp
  and and_1 (and_1_out, out_11, out_13);
  Hex_Digit_Display hex_digit_display_3 (.value({out_9, out_8, out_7, out_6}));  // open: dp
  Clock clock_4 (.out(clock_4_out));
  J_K_Flip_Flop #(.trigger("falling")) j_k_ff_13 (
    .J(1'b1), .clk(clock_4_out), .K(1'b1), .Q(out_14), .reset(and_2_out));  // open: Qn, preset, en
  J_K_Flip_Flop #(.trigger("falling")) j_k_ff_14 (
    .J(1'b1), .clk(out_14), .K(1'b1), .Q(out_15), .reset(and_2_out));  // open: Qn, preset, en
  J_K_Flip_Flop #(.trigger("falling")) j_k_ff_15 (
    .J(1'b1), .clk(out_15), .K(1'b1), .Q(out_16), .reset(and_2_out));  // open: Qn, preset, en
  J_K_Flip_Flop #(.trigger("falling")) j_k_ff_16 (
    .J(1'b1), .clk(out_16), .K(1'b1), .Q(out_17), .reset(and_2_out));  // open: Qn, preset, en
  Hex_Digit_Display hex_digit_display_4 (.value({out_17, out_16, out_15, out_14}));  // open: dp
  and and_2 (and_2_out, out_15, out_17, out_14);

  // Notes on the sheet:
  //   1 : 하향
  //   4bit 비동기식 상향 카운터
  //   4bit 비동기식 상향/하향 카운터
  //   비동기식 BCD 상향 카운터
  //   비동기식 11진 상향 카운터
endmodule
