// Logisim project comparator.circ as structural Verilog: 2 circuits, main circuit 4bit 비교기
module \_4bit_비교기  (
  input  [3:0] A,
  input  [3:0] B,
  input  Input_bigger,
  input  Input_smaller,
  input  Input_same,
  output Output_bigger,
  output Output_smaller,
  output Output_same
);

  wire \n1bit_비교기_1_output_bigger , \n1bit_비교기_1_output_same , \n1bit_비교기_1_output_smaller ,
       \n1bit_비교기_2_output_bigger , \n1bit_비교기_2_output_same , \n1bit_비교기_2_output_smaller ,
       \n1bit_비교기_3_output_bigger , \n1bit_비교기_3_output_same , \n1bit_비교기_3_output_smaller ;

  LED led_1 (.in(A[3]));
  LED led_2 (.in(B[3]));
  LED led_3 (.in(A[1]));
  LED led_4 (.in(A[0]));
  LED led_5 (.in(A[2]));
  LED led_6 (.in(B[0]));
  LED led_7 (.in(B[2]));
  LED led_8 (.in(B[1]));
  \_1bit_비교기  \u_1bit_비교기_1  (
    .Input_bigger(Input_bigger), .Input_smaller(Input_smaller), .Input_same(Input_same), .A(A[3]), .B(B[3]),
    .Output_bigger(\n1bit_비교기_1_output_bigger ), .Output_smaller(\n1bit_비교기_1_output_smaller ),
    .Output_same(\n1bit_비교기_1_output_same ));
  \_1bit_비교기  \u_1bit_비교기_2  (
    .Input_bigger(\n1bit_비교기_1_output_bigger ), .Input_smaller(\n1bit_비교기_1_output_smaller ),
    .Input_same(\n1bit_비교기_1_output_same ), .A(A[2]), .B(B[2]), .Output_bigger(\n1bit_비교기_2_output_bigger ),
    .Output_smaller(\n1bit_비교기_2_output_smaller ), .Output_same(\n1bit_비교기_2_output_same ));
  LED led_9 (.in(Output_smaller));
  LED led_10 (.in(Output_bigger));
  \_1bit_비교기  \u_1bit_비교기_3  (
    .Input_bigger(\n1bit_비교기_2_output_bigger ), .Input_smaller(\n1bit_비교기_2_output_smaller ),
    .Input_same(\n1bit_비교기_2_output_same ), .A(A[1]), .B(B[1]), .Output_bigger(\n1bit_비교기_3_output_bigger ),
    .Output_smaller(\n1bit_비교기_3_output_smaller ), .Output_same(\n1bit_비교기_3_output_same ));
  LED led_11 (.in(Output_same));
  \_1bit_비교기  \u_1bit_비교기_4  (
    .Input_bigger(\n1bit_비교기_3_output_bigger ), .Input_smaller(\n1bit_비교기_3_output_smaller ),
    .Input_same(\n1bit_비교기_3_output_same ), .A(A[0]), .B(B[0]), .Output_bigger(Output_bigger),
    .Output_smaller(Output_smaller), .Output_same(Output_same));

  // Notes on the sheet:
  //   A
  //   B
  //   A>B
  //   A<B
  //   A=B
endmodule

module \_1bit_비교기  (
  input  A,
  input  B,
  input  Input_bigger,
  input  Input_smaller,
  input  Input_same,
  output Output_bigger,
  output Output_smaller,
  output Output_same
);

  wire and_1_out, and_2_out, xnor_1_out;

  xnor xnor_1 (xnor_1_out, A, B);
  and and_1 (and_1_out, Input_same, A, ~B);  // AND_Gate
  and and_2 (and_2_out, Input_same, B, ~A);  // AND_Gate
  or or_1 (Output_bigger, and_1_out, Input_bigger);
  or or_2 (Output_smaller, and_2_out, Input_smaller);
  and and_3 (Output_same, xnor_1_out, Input_same);
endmodule
