// Logisim project latch and flip-flop.circ as structural Verilog: 2 circuits, main circuit main
module main (
  input  R,
  input  S,
  input  Enable,
  input  R_2,
  input  S_2,
  input  S_3,
  input  S_4,
  input  R_3,
  input  R_4,
  input  D,
  input  D_2,
  input  J,
  input  J_2,
  input  K,
  input  K_2,
  input  T,
  input  T_2,
  output Q,
  output Q_2,
  output nQ,
  output nQ_2,
  output Q_3,
  output Q_4,
  output nQ_3,
  output nQ_4,
  output Q_5,
  output Q_6,
  output nQ_5,
  output nQ_6,
  output Q_7,
  output Q_8,
  output nQ_7,
  output nQ_8,
  output Q_9,
  output Q_10,
  output nQ_9,
  output nQ_10
);

  wire clock_1_out, clock_2_out, clock_3_out, clock_4_out, clock_5_out, clock_6_out, clock_7_out,
       clock_8_out, nand_1_out, nand_2_out;

  Clock clock_1 (.out(clock_1_out));
  Clock clock_2 (.out(clock_2_out));
  Clock clock_3 (.out(clock_3_out));
  Clock clock_4 (.out(clock_4_out));
  nor G1 (Q, R, nQ_2);
  nor G1_2 (nQ_2, Q, S_2);
  S_R_Flip_Flop SR_F_F_Rising (.S(S_3), .clk(clock_1_out), .R(R_3), .Q(Q_3), .Qn(nQ_3));  // open: preset, reset, en
  D_Flip_Flop D_F_F_Rising (.clk(clock_2_out), .D(D_2), .Q(Q_6), .Qn(nQ_6));  // open: preset, en, reset
  J_K_Flip_Flop JK_F_F_Rising (.J(J), .clk(clock_3_out), .K(K), .Q(Q_7), .Qn(nQ_7));  // open: preset, en, reset
  T_Flip_Flop T_F_F_Rising (.clk(clock_4_out), .T(T), .Q(Q_9), .Qn(nQ_9));  // open: preset, reset, en
  Clock clock_5 (.out(clock_5_out));
  Clock clock_6 (.out(clock_6_out));
  Clock clock_7 (.out(clock_7_out));
  Clock clock_8 (.out(clock_8_out));
  S_R_Flip_Flop #(.trigger("falling")) SR_F_F_Falling (
    .S(S_4), .clk(clock_5_out), .R(R_4), .Q(Q_4), .Qn(nQ_4));  // open: preset, reset, en
  D_Flip_Flop #(.trigger("falling")) D_F_F_Falling (
    .clk(clock_6_out), .D(D), .Q(Q_5), .Qn(nQ_5));  // open: preset, en, reset
  J_K_Flip_Flop #(.trigger("falling")) JK_F_F_Falling (
    .J(J_2), .clk(clock_7_out), .K(K_2), .Q(Q_8), .Qn(nQ_8));  // open: preset, en, reset
  T_Flip_Flop #(.trigger("falling")) T_F_F_Falling (
    .clk(clock_8_out), .T(T_2), .Q(Q_10), .Qn(nQ_10));  // open: preset, reset, en
  nand nand_1 (nand_1_out, S, Enable);
  nand nand_2 (nand_2_out, Enable, R_2);
  nand nand_3 (Q_2, nand_1_out, nQ);
  nand nand_4 (nQ, Q_2, nand_2_out);

  // Notes on the sheet:
  //   NOR Gate SR Latch
  //   Gated SR Latch
endmodule

module FF (
  input  S,
  input  R,
  input  PRESET,
  input  CLEAR,
  output out_5,
  output out_6,
  output out_7,
  output out_8,
  output out_9,
  output out_10,
  output out_11
);

  wire clock_1_out, clock_2_out, clock_3_out, clock_4_out, clock_5_out, clock_6_out, clock_7_out, d_ff_1_qn,
       d_ff_2_q, d_ff_2_qn, d_ff_3_q, d_ff_3_qn, d_ff_4_qn, j_k_ff_1_qn, j_k_ff_3_q, j_k_ff_4_q, t_ff_1_q,
       t_ff_2_q;

  Clock clock_1 (.out(clock_1_out));
  Clock clock_2 (.out(clock_2_out));
  J_K_Flip_Flop j_k_ff_1 (
    .J(j_k_ff_1_qn), .clk(clock_1_out), .K(out_9), .Q(out_9), .Qn(j_k_ff_1_qn));  // open: preset, en, reset
  D_Flip_Flop d_ff_1 (.clk(clock_2_out), .D(d_ff_1_qn), .Q(out_7), .Qn(d_ff_1_qn));  // open: preset, en, reset
  Clock clock_3 (.out(clock_3_out));
  J_K_Flip_Flop j_k_ff_2 (.J(1'b1), .clk(clock_3_out), .K(1'b1), .Q(out_10));  // open: Qn, preset, en, reset
  LED led_1 (.in(clock_4_out));
  Clock clock_4 (.out(clock_4_out));
  Clock clock_5 (.out(clock_5_out));
  LED led_2 (.in(clock_5_out));
  LED led_3 (.in(clock_6_out));
  Clock clock_6 (.out(clock_6_out));
  LED led_4 (.in(t_ff_1_q));
  T_Flip_Flop t_ff_1 (.clk(clock_4_out), .T(1'b1), .Q(t_ff_1_q));  // open: Qn, preset, reset, en
  LED led_5 (.in(d_ff_2_q));
  D_Flip_Flop d_ff_2 (.clk(clock_5_out), .D(d_ff_2_qn), .Q(d_ff_2_q), .Qn(d_ff_2_qn));  // open: preset, en, reset
  LED led_6 (.in(j_k_ff_3_q));
  J_K_Flip_Flop j_k_ff_3 (.J(1'b1), .clk(clock_6_out), .K(1'b1), .Q(j_k_ff_3_q));  // open: Qn, preset, en, reset
  LED led_7 (.in(t_ff_2_q));
  T_Flip_Flop t_ff_2 (.clk(t_ff_1_q), .T(1'b1), .Q(t_ff_2_q));  // open: Qn, preset, reset, en
  LED led_8 (.in(d_ff_3_q));
  D_Flip_Flop d_ff_3 (.clk(d_ff_2_q), .D(d_ff_3_qn), .Q(d_ff_3_q), .Qn(d_ff_3_qn));  // open: preset, en, reset
  LED led_9 (.in(j_k_ff_4_q));
  J_K_Flip_Flop j_k_ff_4 (.J(1'b1), .clk(j_k_ff_3_q), .K(1'b1), .Q(j_k_ff_4_q));  // open: Qn, preset, en, reset
  LED led_10 (.in(out_8));
  D_Flip_Flop d_ff_4 (.clk(d_ff_3_q), .D(d_ff_4_qn), .Q(out_8), .Qn(d_ff_4_qn));  // open: preset, en, reset
  LED led_11 (.in(out_11));
  J_K_Flip_Flop j_k_ff_5 (.J(1'b1), .clk(j_k_ff_4_q), .K(1'b1), .Q(out_11));  // open: Qn, preset, en, reset
  LED led_12 (.in(out_5));
  T_Flip_Flop t_ff_3 (.clk(t_ff_2_q), .T(1'b1), .Q(out_5));  // open: Qn, preset, reset, en
  Clock clock_7 (.out(clock_7_out));
  S_R_Flip_Flop s_r_ff_1 (.S(S), .clk(clock_7_out), .R(R), .Q(out_6), .preset(PRESET), .reset(CLEAR));  // open: Qn, en

  // Notes on the sheet:
  //   T-FF의 구현(JK-FF를 이용)
  //   T-FF의 구현(D-FF를 이용)
  //   T-FF를 이용한 주파수 감소회로
  //   비동기 입력을 갖는 SR-FF
endmodule
