// Logisim project Tutorial.circ as structural Verilog: 1 circuit, main circuit main
module main (
  input  in_1,
  input  in_2,
  output out_3,
  output out_4,
  output out_5,
  output out_6,
  output out_7,
  output out_8,
  output out_9,
  output out_10,
  output out_11,
  output out_12,
  output out_13,
  output out_14,
  output out_15,
  output out_16,
  output out_17,
  output out_18,
  output out_19,
  output out_20,
  output out_21,
  output out_22,
  output out_23,
  output out_24,
  output out_25,
  output out_26
);

  LED led_1 (.in(in_2));
  LED led_2 (.in(in_1));
  and and_1 (out_3, in_1, in_2);
  or or_1 (out_5, in_1, in_2);
  nor nor_1 (out_7, in_1, in_2);
  LED led_3 (.in(out_3));
  LED led_4 (.in(out_7));
  nand nand_1 (out_9, out_7, out_3);
  xor xor_1 (out_11, out_7, out_3);
  xnor xnor_1 (out_13, out_7, out_3);
  LED led_5 (.in(out_11));
  LED led_6 (.in(in_2));
  LED led_7 (.in(out_9));
  LED led_8 (.in(in_1));
  and and_2 (out_15, out_9, out_11);
  or or_2 (out_17, out_9, out_11);
  nor nor_2 (out_19, out_9, out_11);
  nand nand_2 (out_4, in_1, in_2);
  xor xor_2 (out_6, in_1, in_2);
  xnor xnor_2 (out_8, in_1, in_2);
  LED led_9 (.in(out_19));
  LED led_10 (.in(out_8));
  LED led_11 (.in(out_6));
  LED led_12 (.in(out_15));
  and and_3 (out_10, out_8, out_6);
  or or_3 (out_12, out_8, out_6);
  nor nor_3 (out_14, out_8, out_6);
  nand nand_3 (out_21, out_15, out_19);
  xor xor_3 (out_23, out_15, out_19);
  xnor xnor_3 (out_25, out_15, out_19);
  LED led_13 (.in(out_10));
  LED led_14 (.in(out_12));
  nand nand_4 (out_16, out_12, out_10);
  xor xor_4 (out_18, out_12, out_10);
  xnor xnor_4 (out_20, out_12, out_10);
  LED led_15 (.in(out_20));
  LED led_16 (.in(out_16));
  and and_4 (out_22, out_20, out_16);
  or or_4 (out_24, out_20, out_16);
  nor nor_4 (out_26, out_20, out_16);
endmodule
