// Logisim project Parallel-adder-subtracter.circ as structural Verilog: 2 circuits, main circuit main
module main (
  input  A3,
  input  B3,
  input  A2,
  input  B2,
  input  A1,
  input  B1,
  input  A0,
  input  B0,
  input  A3_2,
  input  B3_2,
  input  A2_2,
  input  B2_2,
  input  A1_2,
  input  B1_2,
  input  A0_2,
  input  B0_2,
  input  Sign,
  output S3,
  output S3_2,
  output S3_3,
  output S3_4,
  output overflow,
  output S3_5,
  output S3_6,
  output S3_7,
  output S3_8,
  output overflow_2
);

  wire adder_1_cout, adder_2_cout, adder_3_cout, adder_4_cout, adder_5_cout, adder_6_cout, adder_7_cout,
       adder_8_cout, xor_3_out, xor_4_out, xor_5_out, xor_6_out;

  xor xor_1 (overflow, adder_1_cout, adder_3_cout);
  xor xor_2 (overflow_2, adder_2_cout, adder_4_cout);
  xor xor_3 (xor_3_out, B3_2, Sign);
  Adder #(.width(1)) adder_1 (.a(B3), .b(A3), .out(S3), .cin(adder_3_cout), .cout(adder_1_cout));
  Adder #(.width(1)) adder_2 (.a(xor_3_out), .b(A3_2), .out(S3_5), .cin(adder_4_cout), .cout(adder_2_cout));
  xor xor_4 (xor_4_out, B2_2, Sign);
  Adder #(.width(1)) adder_3 (.a(B2), .b(A2), .out(S3_2), .cin(adder_5_cout), .cout(adder_3_cout));
  Adder #(.width(1)) adder_4 (.a(xor_4_out), .b(A2_2), .out(S3_6), .cin(adder_6_cout), .cout(adder_4_cout));
  xor xor_5 (xor_5_out, B1_2, Sign);
  Adder #(.width(1)) adder_5 (.a(B1), .b(A1), .out(S3_3), .cin(adder_7_cout), .cout(adder_5_cout));
  Adder #(.width(1)) adder_6 (.a(xor_5_out), .b(A1_2), .out(S3_7), .cin(adder_8_cout), .cout(adder_6_cout));
  Adder #(.width(1)) adder_7 (.a(B0), .b(A0), .out(S3_4), .cin(1'b0), .cout(adder_7_cout));
  xor xor_6 (xor_6_out, B0_2, Sign);
  Adder #(.width(1)) adder_8 (.a(xor_6_out), .b(A0_2), .out(S3_8), .cin(Sign), .cout(adder_8_cout));

  // Notes on the sheet:
  //   0 : ADD, 1 : SUB
  //   Parallel-adder
  //   Parallel-adder/subtracter
endmodule

module \_4bit_병렬감가산기  (
  input  [3:0] in_1,
  input  [3:0] in_2,
  input  Sign,
  output overflow,
  output Zero,
  output S3,
  output S3_2,
  output S3_3,
  output S3_4,
  output Carry
);

  wire adder_2_cout, adder_3_cout, adder_4_cout, xor_2_out, xor_3_out, xor_4_out, xor_5_out;

  xor xor_1 (overflow, Carry, adder_2_cout);
  and and_1 (Zero, ~S3, ~S3_2, ~S3_3, ~S3_4);  // AND_Gate
  xor xor_2 (xor_2_out, in_2[3], Sign);
  Adder #(.width(1)) adder_1 (.a(xor_2_out), .b(in_1[3]), .out(S3), .cin(adder_2_cout), .cout(Carry));
  xor xor_3 (xor_3_out, in_2[2], Sign);
  Adder #(.width(1)) adder_2 (.a(xor_3_out), .b(in_1[2]), .out(S3_2), .cin(adder_3_cout), .cout(adder_2_cout));
  xor xor_4 (xor_4_out, in_2[1], Sign);
  Adder #(.width(1)) adder_3 (.a(xor_4_out), .b(in_1[1]), .out(S3_3), .cin(adder_4_cout), .cout(adder_3_cout));
  xor xor_5 (xor_5_out, in_2[0], Sign);
  Adder #(.width(1)) adder_4 (.a(xor_5_out), .b(in_1[0]), .out(S3_4), .cin(Sign), .cout(adder_4_cout));
  Hex_Digit_Display hex_digit_display_1 (.value({S3, S3_2, S3_3, S3_4}));  // open: dp

  // Notes on the sheet:
  //   0 : ADD, 1 : SUB
  //   Parallel-adder/subtracter
endmodule
