// Logisim project Register-Counter.circ as structural Verilog: 1 circuit, main circuit main
module main (
  input  in_1,
  input  READ,
  input  in_3,
  input  INIT_Active_High,
  input  B3,
  input  B2,
  input  B1,
  input  B0,
  input  SH_nLD,
  input  I3,
  input  I2,
  input  I1,
  input  I0,
  input  WR,
  input  INIT__Active_High,
  input  READ_2,
  output QA,
  output QB,
  output QC,
  output QD,
  output B3_2,
  output B2_2,
  output B1_2,
  output B0_2,
  output out_25,
  output QA__MSB,
  output QB_2,
  output QC_2,
  output QD__LSB,
  output O3,
  output O2,
  output O1,
  output O0,
  output out_34,
  output out_35,
  output out_36,
  output out_37,
  output out_38,
  output out_39,
  output out_40,
  output out_41
);

  wire and_1_out, and_2_out, and_3_out, and_4_out, clock_1_out, clock_2_out, clock_3_out, clock_4_out,
       clock_5_out, d_ff_1_q, d_ff_2_q, d_ff_3_q, d_ff_4_q, d_ff_5_q, d_ff_6_q, d_ff_7_q, d_ff_8_q, d_ff_9_q,
       d_ff_10_q, d_ff_11_q, d_ff_13_qn, d_ff_16_qn, d_ff_18_qn, d_ff_20_qn, multiplexer_1_out,
       multiplexer_2_out, multiplexer_3_out;

  Clock clock_1 (.out(clock_1_out));
  Clock clock_2 (.out(clock_2_out));
  D_Flip_Flop d_ff_1 (.clk(clock_1_out), .D(in_1), .Q(d_ff_1_q));  // open: Qn, preset, en, reset
  assign B3_2 = READ ? d_ff_1_q : 1'bz;  // Controlled_Buffer controlled_buffer_1
  D_Flip_Flop d_ff_2 (.clk(clock_2_out), .D(B3), .Q(d_ff_2_q));  // open: Qn, preset, en, reset
  and and_1 (and_1_out, WR, I3);
  Clock clock_3 (.out(clock_3_out));
  D_Flip_Flop d_ff_3 (.clk(clock_1_out), .D(d_ff_1_q), .Q(d_ff_3_q));  // open: Qn, preset, en, reset
  assign B2_2 = READ ? d_ff_3_q : 1'bz;  // Controlled_Buffer controlled_buffer_2
  Multiplexer multiplexer_1 (.in0(B2), .in1(d_ff_2_q), .out(multiplexer_1_out), .sel(SH_nLD));  // open: en
  D_Flip_Flop d_ff_4 (.clk(clock_2_out), .D(multiplexer_1_out), .Q(d_ff_4_q));  // open: Qn, preset, en, reset
  and and_2 (and_2_out, WR, I2);
  D_Flip_Flop d_ff_5 (.clk(clock_3_out), .D(and_1_out), .Q(d_ff_5_q));  // open: Qn, preset, en, reset
  assign O3 = READ_2 ? d_ff_5_q : 1'bz;  // Controlled_Buffer controlled_buffer_3
  D_Flip_Flop d_ff_6 (.clk(clock_1_out), .D(d_ff_3_q), .Q(d_ff_6_q));  // open: Qn, preset, en, reset
  assign B1_2 = READ ? d_ff_6_q : 1'bz;  // Controlled_Buffer controlled_buffer_4
  Multiplexer multiplexer_2 (.in0(B1), .in1(d_ff_4_q), .out(multiplexer_2_out), .sel(SH_nLD));  // open: en
  and and_3 (and_3_out, WR, I1);
  D_Flip_Flop d_ff_7 (.clk(clock_3_out), .D(and_2_out), .Q(d_ff_7_q));  // open: Qn, preset, en, reset
  assign O2 = READ_2 ? d_ff_7_q : 1'bz;  // Controlled_Buffer controlled_buffer_5
  D_Flip_Flop d_ff_8 (.clk(clock_1_out), .D(d_ff_6_q), .Q(d_ff_8_q));  // open: Qn, preset, en, reset
  assign B0_2 = READ ? d_ff_8_q : 1'bz;  // Controlled_Buffer controlled_buffer_6
  D_Flip_Flop d_ff_9 (.clk(clock_2_out), .D(multiplexer_2_out), .Q(d_ff_9_q));  // open: Qn, preset, en, reset
  and and_4 (and_4_out, WR, I0);
  D_Flip_Flop d_ff_10 (.clk(clock_3_out), .D(and_3_out), .Q(d_ff_10_q));  // open: Qn, preset, en, reset
  assign O1 = READ_2 ? d_ff_10_q : 1'bz;  // Controlled_Buffer controlled_buffer_7
  Multiplexer multiplexer_3 (.in0(B0), .in1(d_ff_9_q), .out(multiplexer_3_out), .sel(SH_nLD));  // open: en
  D_Flip_Flop d_ff_11 (.clk(clock_3_out), .D(and_4_out), .Q(d_ff_11_q));  // open: Qn, preset, en, reset
  assign O0 = READ_2 ? d_ff_11_q : 1'bz;  // Controlled_Buffer controlled_buffer_8
  D_Flip_Flop d_ff_12 (.clk(clock_2_out), .D(multiplexer_3_out), .Q(out_25));  // open: Qn, preset, en, reset
  Clock clock_4 (.out(clock_4_out));
  Clock clock_5 (.out(clock_5_out));
  D_Flip_Flop d_ff_13 (
    .clk(clock_4_out), .D(d_ff_20_qn), .Q(QA__MSB), .Qn(d_ff_13_qn), .reset(INIT__Active_High));  // open: preset, en
  and and_5 (out_34, QA__MSB, d_ff_16_qn);
  and and_6 (out_35, QB_2, d_ff_18_qn);
  D_Flip_Flop d_ff_14 (.clk(clock_5_out), .D(QD), .Q(QA), .preset(in_3));  // open: Qn, en, reset
  and and_7 (out_36, QC_2, d_ff_20_qn);
  D_Flip_Flop d_ff_15 (.clk(clock_5_out), .D(QA), .Q(QB), .reset(INIT_Active_High));  // open: Qn, preset, en
  D_Flip_Flop d_ff_16 (
    .clk(clock_4_out), .D(QA__MSB), .Q(QB_2), .Qn(d_ff_16_qn), .reset(INIT__Active_High));  // open: preset, en
  and and_8 (out_37, QA__MSB, QD__LSB);
  D_Flip_Flop d_ff_17 (.clk(clock_5_out), .D(QB), .Q(QC), .reset(INIT_Active_High));  // open: Qn, preset, en
  D_Flip_Flop d_ff_18 (
    .clk(clock_4_out), .D(QB_2), .Q(QC_2), .Qn(d_ff_18_qn), .reset(INIT__Active_High));  // open: preset, en
  and and_9 (out_38, d_ff_13_qn, QB_2);
  and and_10 (out_39, d_ff_16_qn, QC_2);
  D_Flip_Flop d_ff_19 (.clk(clock_5_out), .D(QC), .Q(QD), .reset(INIT_Active_High));  // open: Qn, preset, en
  D_Flip_Flop d_ff_20 (
    .clk(clock_4_out), .D(QC_2), .Q(QD__LSB), .Qn(d_ff_20_qn), .reset(INIT__Active_High));  // open: preset, en
  and and_11 (out_40, d_ff_18_qn, QD__LSB);
  and and_12 (out_41, d_ff_13_qn, d_ff_20_qn);

  // Notes on the sheet:
  //   4bit SIPO Register
  //   4bit PISO Register
  //   4bit PIPO Register
  //   4bit Ring Counter
endmodule
