// Logisim project digital clock - 2013154012 김한상.circ as structural Verilog: 1 circuit, main circuit main
module main (
  input  in_1,
  input  in_2,
  input  in_3,
  input  in_4
);

  wire and_1_out, and_2_out, and_3_out, and_4_out, and_5_out, and_6_out, clock_1_out,
       controlled_buffer_1_out, controlled_buffer_3_out, controlled_buffer_5_out, controlled_buffer_7_out,
       controlled_buffer_9_out, controlled_buffer_11_out, controlled_buffer_13_out, controlled_buffer_15_out,
       j_k_ff_2_qn, j_k_ff_3_qn, j_k_ff_4_qn, j_k_ff_6_qn, j_k_ff_8_qn, j_k_ff_11_qn, j_k_ff_12_qn,
       j_k_ff_13_qn, j_k_ff_16_qn, j_k_ff_19_qn, j_k_ff_20_qn, j_k_ff_21_qn, j_k_ff_24_qn, not_1_out;
  wire [3:0] j_k_ff_1_q, j_k_ff_2_q, j_k_ff_9_q, j_k_ff_10_q, j_k_ff_17_q, j_k_ff_18_q;

  and and_1 (and_1_out, ~j_k_ff_3_qn, ~j_k_ff_6_qn, ~j_k_ff_2_qn);  // AND_Gate
  assign controlled_buffer_1_out = not_1_out ? and_3_out : 1'bz;  // Controlled_Buffer controlled_buffer_1
  assign controlled_buffer_1_out = in_1 ? in_2 : 1'bz;  // Controlled_Buffer controlled_buffer_2
  assign controlled_buffer_3_out = and_1_out ? and_1_out : 1'bz;  // Controlled_Buffer controlled_buffer_3
  J_K_Flip_Flop #(.trigger("falling")) j_k_ff_1 (
    .J(1'b1), .clk(and_2_out), .K(1'b1), .Q(j_k_ff_1_q[0]), .reset(and_1_out));  // open: Qn, preset, en
  J_K_Flip_Flop #(.trigger("falling")) j_k_ff_2 (
    .J(1'b1), .clk(controlled_buffer_1_out), .K(1'b1), .Q(j_k_ff_2_q[0]), .Qn(j_k_ff_2_qn),
    .reset(controlled_buffer_3_out));  // open: preset, en
  assign controlled_buffer_3_out = and_2_out ? and_2_out : 1'bz;  // Controlled_Buffer controlled_buffer_4
  and and_2 (and_2_out, ~j_k_ff_4_qn, ~j_k_ff_8_qn);  // AND_Gate
  J_K_Flip_Flop #(.trigger("falling")) j_k_ff_3 (
    .J(1'b1), .clk(j_k_ff_1_q[0]), .K(1'b1), .Q(j_k_ff_1_q[1]), .Qn(j_k_ff_3_qn), .reset(and_1_out));  // open: preset, en
  J_K_Flip_Flop #(.trigger("falling")) j_k_ff_4 (
    .J(1'b1), .clk(j_k_ff_2_q[0]), .K(1'b1), .Q(j_k_ff_2_q[1]), .Qn(j_k_ff_4_qn),
    .reset(controlled_buffer_3_out));  // open: preset, en
  J_K_Flip_Flop #(.trigger("falling")) j_k_ff_5 (
    .J(1'b1), .clk(j_k_ff_1_q[1]), .K(1'b1), .Q(j_k_ff_1_q[2]), .reset(and_1_out));  // open: Qn, preset, en
  J_K_Flip_Flop #(.trigger("falling")) j_k_ff_6 (
    .J(1'b1), .clk(j_k_ff_2_q[1]), .K(1'b1), .Q(j_k_ff_2_q[2]), .Qn(j_k_ff_6_qn),
    .reset(controlled_buffer_3_out));  // open: preset, en
  J_K_Flip_Flop #(.trigger("falling")) j_k_ff_7 (
    .J(1'b1), .clk(j_k_ff_1_q[2]), .K(1'b1), .Q(j_k_ff_1_q[3]), .reset(and_1_out));  // open: Qn, preset, en
  assign controlled_buffer_5_out = not_1_out ? and_5_out : 1'bz;  // Controlled_Buffer controlled_buffer_5
  assign controlled_buffer_5_out = in_1 ? in_3 : 1'bz;  // Controlled_Buffer controlled_buffer_6
  J_K_Flip_Flop #(.trigger("falling")) j_k_ff_8 (
    .J(1'b1), .clk(j_k_ff_2_q[2]), .K(1'b1), .Q(j_k_ff_2_q[3]), .Qn(j_k_ff_8_qn),
    .reset(controlled_buffer_3_out));  // open: preset, en
  J_K_Flip_Flop #(.trigger("falling")) j_k_ff_9 (
    .J(1'b1), .clk(and_4_out), .K(1'b1), .Q(j_k_ff_9_q[0]), .reset(controlled_buffer_7_out));  // open: Qn, preset, en
  assign controlled_buffer_7_out = and_1_out ? and_1_out : 1'bz;  // Controlled_Buffer controlled_buffer_7
  assign controlled_buffer_7_out = and_3_out ? and_3_out : 1'bz;  // Controlled_Buffer controlled_buffer_8
  J_K_Flip_Flop #(.trigger("falling")) j_k_ff_10 (
    .J(1'b1), .clk(controlled_buffer_5_out), .K(1'b1), .Q(j_k_ff_10_q[0]), .reset(controlled_buffer_9_out));  // open: Qn, preset, en
  assign controlled_buffer_9_out = and_4_out ? and_4_out : 1'bz;  // Controlled_Buffer controlled_buffer_9
  assign controlled_buffer_9_out = and_1_out ? and_1_out : 1'bz;  // Controlled_Buffer controlled_buffer_10
  J_K_Flip_Flop #(.trigger("falling")) j_k_ff_11 (
    .J(1'b1), .clk(j_k_ff_9_q[0]), .K(1'b1), .Q(j_k_ff_9_q[1]), .Qn(j_k_ff_11_qn),
    .reset(controlled_buffer_7_out));  // open: preset, en
  and and_3 (and_3_out, ~j_k_ff_11_qn, ~j_k_ff_13_qn);  // AND_Gate
  J_K_Flip_Flop #(.trigger("falling")) j_k_ff_12 (
    .J(1'b1), .clk(j_k_ff_10_q[0]), .K(1'b1), .Q(j_k_ff_10_q[1]), .Qn(j_k_ff_12_qn),
    .reset(controlled_buffer_9_out));  // open: preset, en
  and and_4 (and_4_out, ~j_k_ff_12_qn, ~j_k_ff_16_qn);  // AND_Gate
  Hex_Digit_Display hex_digit_display_1 (.value(j_k_ff_2_q), .dp(clock_1_out));
  Hex_Digit_Display hex_digit_display_2 (.value(j_k_ff_1_q));  // open: dp
  J_K_Flip_Flop #(.trigger("falling")) j_k_ff_13 (
    .J(1'b1), .clk(j_k_ff_9_q[1]), .K(1'b1), .Q(j_k_ff_9_q[2]), .Qn(j_k_ff_13_qn),
    .reset(controlled_buffer_7_out));  // open: preset, en
  J_K_Flip_Flop #(.trigger("falling")) j_k_ff_14 (
    .J(1'b1), .clk(j_k_ff_10_q[1]), .K(1'b1), .Q(j_k_ff_10_q[2]), .reset(controlled_buffer_9_out));  // open: Qn, preset, en
  Hex_Digit_Display hex_digit_display_3 (.value(j_k_ff_10_q), .dp(clock_1_out));
  Hex_Digit_Display hex_digit_display_4 (.value(j_k_ff_9_q));  // open: dp
  J_K_Flip_Flop #(.trigger("falling")) j_k_ff_15 (
    .J(1'b1), .clk(j_k_ff_9_q[2]), .K(1'b1), .Q(j_k_ff_9_q[3]), .reset(controlled_buffer_7_out));  // open: Qn, preset, en
  J_K_Flip_Flop #(.trigger("falling")) j_k_ff_16 (
    .J(1'b1), .clk(j_k_ff_10_q[2]), .K(1'b1), .Q(j_k_ff_10_q[3]), .Qn(j_k_ff_16_qn),
    .reset(controlled_buffer_9_out));  // open: preset, en
  Hex_Digit_Display hex_digit_display_5 (.value(j_k_ff_17_q));  // open: dp
  assign controlled_buffer_11_out = not_1_out ? clock_1_out : 1'bz;  // Controlled_Buffer controlled_buffer_11
  assign controlled_buffer_11_out = in_1 ? in_4 : 1'bz;  // Controlled_Buffer controlled_buffer_12
  Hex_Digit_Display hex_digit_display_6 (.value(j_k_ff_18_q), .dp(clock_1_out));
  J_K_Flip_Flop #(.trigger("falling")) j_k_ff_17 (
    .J(1'b1), .clk(and_6_out), .K(1'b1), .Q(j_k_ff_17_q[0]), .reset(controlled_buffer_13_out));  // open: Qn, preset, en
  assign controlled_buffer_13_out = and_1_out ? and_1_out : 1'bz;  // Controlled_Buffer controlled_buffer_13
  assign controlled_buffer_13_out = and_5_out ? and_5_out : 1'bz;  // Controlled_Buffer controlled_buffer_14
  not not_1 (not_1_out, in_1);
  J_K_Flip_Flop #(.trigger("falling")) j_k_ff_18 (
    .J(1'b1), .clk(controlled_buffer_11_out), .K(1'b1), .Q(j_k_ff_18_q[0]), .reset(controlled_buffer_15_out));  // open: Qn, preset, en
  assign controlled_buffer_15_out = and_6_out ? and_6_out : 1'bz;  // Controlled_Buffer controlled_buffer_15
  J_K_Flip_Flop #(.trigger("falling")) j_k_ff_19 (
    .J(1'b1), .clk(j_k_ff_17_q[0]), .K(1'b1), .Q(j_k_ff_17_q[1]), .Qn(j_k_ff_19_qn),
    .reset(controlled_buffer_13_out));  // open: preset, en
  and and_5 (and_5_out, ~j_k_ff_19_qn, ~j_k_ff_21_qn);  // AND_Gate
  J_K_Flip_Flop #(.trigger("falling")) j_k_ff_20 (
    .J(1'b1), .clk(j_k_ff_18_q[0]), .K(1'b1), .Q(j_k_ff_18_q[1]), .Qn(j_k_ff_20_qn),
    .reset(controlled_buffer_15_out));  // open: preset, en
  and and_6 (and_6_out, ~j_k_ff_20_qn, ~j_k_ff_24_qn);  // AND_Gate
  assign controlled_buffer_15_out = and_1_out ? and_1_out : 1'bz;  // Controlled_Buffer controlled_buffer_16
  J_K_Flip_Flop #(.trigger("falling")) j_k_ff_21 (
    .J(1'b1), .clk(j_k_ff_17_q[1]), .K(1'b1), .Q(j_k_ff_17_q[2]), .Qn(j_k_ff_21_qn),
    .reset(controlled_buffer_13_out));  // open: preset, en
  J_K_Flip_Flop #(.trigger("falling")) j_k_ff_22 (
    .J(1'b1), .clk(j_k_ff_18_q[1]), .K(1'b1), .Q(j_k_ff_18_q[2]), .reset(controlled_buffer_15_out));  // open: Qn, preset, en
  J_K_Flip_Flop #(.trigger("falling")) j_k_ff_23 (
    .J(1'b1), .clk(j_k_ff_17_q[2]), .K(1'b1), .Q(j_k_ff_17_q[3]), .reset(controlled_buffer_13_out));  // open: Qn, preset, en
  J_K_Flip_Flop #(.trigger("falling")) j_k_ff_24 (
    .J(1'b1), .clk(j_k_ff_18_q[2]), .K(1'b1), .Q(j_k_ff_18_q[3]), .Qn(j_k_ff_24_qn),
    .reset(controlled_buffer_15_out));  // open: preset, en
  Clock clock_1 (.out(clock_1_out));
endmodule
